# Fritzing sketch MB_ServoBoardv2 (saved by Fritzing 0.9.8b)
circuit board: 2.79763cm x 3.49001cm
breadboards: 1

parts:
  µB = Dagu DGServo 9g header (male) [package=THT]
  S1 = Dagu DGServo 9g header (male) [package=THT]
  S2 = Dagu DGServo 9g header (male) [package=THT]
  Batt = male pin header, 2 pins [form="♂ (male)"]

nets:
  GND: µB.gnd, S1.gnd, S2.gnd, Batt.pin1
  N1: µB.Vcc, S1.pulse
  N2: µB.pulse, S2.pulse
  VCC: S1.Vcc, S2.Vcc, Batt.pin2

notes:
  S1
  S2
  GND
